// Logisim project BasicComputer.circ as structural Verilog: 11 circuits, main circuit main
module main (
);

  wire AC_CLR, AC_INR, AC_LD, ADD, AND, and_1_out, and_2_out, AR_CLR, AR_INR, AR_LD, Clk, clock_1_out, COM,
       DR_IN, DR_INR, DR_LD, E, E_CLR, E_COM, E_LD, E_outt, E_qn, FGI, FGI_CLR, FGO, FGO_CLR, IEN, IEN_CLR,
       IEN_SET, INPR, IR_LD, MEM_RD, MEM_WR, or_1_out, or_2_out, OUTR_LD, PC_CLR, PC_INR, PC_LD, R, R_CLR,
       R_SET, S0, S1, S2, S_CLR, S_q, SHL, SHR, TR_LD;
  wire [7:0] bit_extender_3_out, INPR_q;
  wire [11:0] AR_q, bit_extender_1_out, bit_extender_2_out, PC_q;
  wire [15:0] AC, AR, bus_1_f, DR, IR, Mem, n16_bit_alu_1_ac_out, PC, TR;

  D_Flip_Flop S (.clk(Clk), .Q(S_q), .en(1'b1), .reset(S_CLR));  // open: D, Qn, preset
  Bit_Extender #(.in_width(16), .out_width(12)) bit_extender_1 (.in(bus_1_f), .out(bit_extender_1_out));
  _16_bit_ALU u_16_bit_alu_1 (
    .AC(AC), .DR(DR), .AND(AND), .ADD(ADD), .DR_IN(DR_IN), .INPR(INPR_q), .INPR_IN(INPR), .COM(COM),
    .SHR(SHR), .SHL(SHL), .E_IN(E), .AC_OUT(n16_bit_alu_1_ac_out), .E_OUT(E_outt));
  and and_1 (and_1_out, E_qn, E_COM);
  Clock clock_1 (.out(clock_1_out));
  Bit_Extender #(.in_width(16), .out_width(12)) bit_extender_2 (.in(bus_1_f), .out(bit_extender_2_out));
  and and_2 (and_2_out, E_LD, E_outt);
  Bit_Extender #(.in_width(16), .out_width(8)) bit_extender_3 (.in(bus_1_f), .out(bit_extender_3_out));
  Control_Unit control_unit_1 (
    .FGO(FGO), .FGI(FGI), .IEN(IEN), .R(R), .E(E), .Clk(Clk), .AC(AC), .DR(DR), .AND(AND), .ADD(ADD),
    .DR_IN(DR_IN), .INPR(INPR), .COM(COM), .SHR(SHR), .SHL(SHL), .IR_LD(IR_LD), .AR_LD(AR_LD), .DR_LD(DR_LD),
    .MEM_WRITE(MEM_WR), .DR_INR(DR_INR), .AR_CLR(AR_CLR), .TR_LD(TR_LD), .AR_INR(AR_INR), .FGI_CLR(FGI_CLR),
    .S0(S0), .S1(S1), .S2(S2), .OUTR_LD(OUTR_LD), .FGO_CLR(FGO_CLR), .PC_LD(PC_LD), .R_SET(R_SET),
    .AC_LD(AC_LD), .E_CLR(E_CLR), .MEM_READ(MEM_RD), .PC_INR(PC_INR), .E_COM(E_COM), .R_CLR(R_CLR),
    .S_CLR(S_CLR), .AC_INR(AC_INR), .IEN_CLR(IEN_CLR), .AC_CLR(AC_CLR), .IEN_SET(IEN_SET), .PC_CLR(PC_CLR),
    .IR(IR), .E_LD(E_LD));
  or or_1 (or_1_out, and_1_out, and_2_out);
  or or_2 (or_2_out, E_COM, E_LD);
  D_Flip_Flop u_IEN (.clk(Clk), .Q(IEN), .preset(IEN_SET), .en(1'b1), .reset(IEN_CLR));  // open: D, Qn
  D_Flip_Flop u_R (.clk(Clk), .Q(R), .preset(R_SET), .en(1'b1), .reset(R_CLR));  // open: D, Qn
  D_Flip_Flop u_FGO (.clk(Clk), .Q(FGO), .en(1'b1), .reset(FGO_CLR));  // open: D, Qn, preset
  D_Flip_Flop u_FGI (.clk(Clk), .Q(FGI), .en(1'b1), .reset(FGI_CLR));  // open: D, Qn, preset
  and and_3 (Clk, clock_1_out, S_q);
  Register u_INPR (.en(1'b1), .Q(INPR_q), .clk(Clk));  // open: D, clr
  Register OUTR (.D(bit_extender_3_out), .en(OUTR_LD), .clk(Clk));  // open: Q, clr
  D_Flip_Flop u_E (.clk(Clk), .D(or_1_out), .Q(E), .Qn(E_qn), .en(or_2_out), .reset(E_CLR));  // open: preset
  RAM #(.addrWidth(12), .dataWidth(16), .bus("separate")) ram_1 (
    .addr(AR_q), .din(bus_1_f), .data(Mem), .str(MEM_WR), .clk(Clk), .ld(MEM_RD));  // open: sel, clr
  _12_bit_Register u_PC (.D(bit_extender_1_out), .Clk(Clk), .Q(PC_q), .CLR(PC_CLR), .LD(PC_LD), .Count(PC_INR));
  _16_bit_Register u_DR (.CLR(1'b0), .LD(DR_LD), .Count(DR_INR), .D(bus_1_f), .Clk(Clk), .Q(DR));
  _16_bit_Register u_AC (.CLR(AC_CLR), .LD(AC_LD), .Count(AC_INR), .D(n16_bit_alu_1_ac_out), .Clk(Clk), .Q(AC));
  _16_bit_Register u_IR (.CLR(1'b0), .LD(IR_LD), .Count(1'b0), .D(bus_1_f), .Clk(Clk), .Q(IR));
  _16_bit_Register u_TR (.CLR(1'b0), .LD(TR_LD), .Count(1'b0), .D(bus_1_f), .Clk(Clk), .Q(TR));
  _12_bit_Register u_AR (.D(bit_extender_2_out), .Clk(Clk), .Q(AR_q), .CLR(AR_CLR), .LD(AR_LD), .Count(AR_INR));
  assign PC = {{4{1'b0}}, PC_q};  // Bit_Extender bit_extender_4
  assign AR = {{4{1'b0}}, AR_q};  // Bit_Extender bit_extender_5
  BUS bus_1 (.R1(AR), .R2(PC), .R3(DR), .F(bus_1_f), .R4(AC), .R5(IR), .S2(S2), .S1(S1), .S0(S0), .R6(TR), .R7(Mem));

  // Notes on the sheet:
  //   Set S
endmodule

module BUS (
  input  [15:0] R1,
  input  [15:0] R2,
  input  [15:0] R3,
  input  [15:0] R4,
  input  [15:0] R5,
  input  S2,
  input  S1,
  input  S0,
  input  [15:0] R6,
  input  [15:0] R7,
  output [15:0] F
);

  Multiplexer #(.select(3), .width(16)) multiplexer_1 (
    .in0({16{1'b0}}), .in1(R1), .in2(R2), .in3(R3), .in4(R4), .in5(R5), .in6(R6), .in7(R7), .out(F),
    .sel({S2, S1, S0}), .en(1'b1));
endmodule

module _1_bit_Register (
  input  CLR,
  input  LD,
  input  Count,
  input  D,
  input  Clk,
  output Q,
  output C_OUT
);

  wire and_1_out, and_2_out, and_3_out, and_4_out, not_1_out, not_2_out, not_3_out, or_1_out, or_2_out;

  not not_1 (not_1_out, CLR);
  not not_2 (not_2_out, D);
  and and_1 (and_1_out, not_1_out, LD);
  not not_3 (not_3_out, LD);
  and and_2 (and_2_out, not_1_out, not_3_out, Count);
  and and_3 (and_3_out, and_1_out, D);
  and and_4 (and_4_out, and_1_out, not_2_out);
  and and_5 (C_OUT, and_2_out, Q);
  or or_1 (or_1_out, and_2_out, and_3_out);
  or or_2 (or_2_out, CLR, and_2_out, and_4_out);
  J_K_Flip_Flop j_k_ff_1 (.J(or_1_out), .clk(Clk), .K(or_2_out), .Q(Q), .en(1'b1));  // open: Qn, preset, reset
endmodule

module _16_bit_Register (
  input  CLR,
  input  Count,
  input  LD,
  input  [15:0] D,
  input  Clk,
  output [15:0] Q
);

  wire n1_bit_register_1_c_out, n1_bit_register_2_c_out, n1_bit_register_3_c_out, n1_bit_register_4_c_out,
       n1_bit_register_5_c_out, n1_bit_register_6_c_out, n1_bit_register_7_c_out, n1_bit_register_8_c_out,
       n1_bit_register_9_c_out, n1_bit_register_10_c_out, n1_bit_register_11_c_out, n1_bit_register_12_c_out,
       n1_bit_register_13_c_out, n1_bit_register_14_c_out, n1_bit_register_15_c_out;

  _1_bit_Register u_1_bit_register_1 (
    .CLR(CLR), .LD(LD), .Count(Count), .D(D[0]), .Q(Q[0]), .Clk(Clk), .C_OUT(n1_bit_register_1_c_out));
  _1_bit_Register u_1_bit_register_2 (
    .CLR(CLR), .LD(LD), .Count(n1_bit_register_13_c_out), .D(D[4]), .Q(Q[4]), .Clk(Clk),
    .C_OUT(n1_bit_register_2_c_out));
  _1_bit_Register u_1_bit_register_3 (
    .CLR(CLR), .LD(LD), .Count(n1_bit_register_14_c_out), .D(D[8]), .Q(Q[8]), .Clk(Clk),
    .C_OUT(n1_bit_register_3_c_out));
  _1_bit_Register u_1_bit_register_4 (
    .CLR(CLR), .LD(LD), .Count(n1_bit_register_15_c_out), .D(D[12]), .Q(Q[12]), .Clk(Clk),
    .C_OUT(n1_bit_register_4_c_out));
  _1_bit_Register u_1_bit_register_5 (
    .CLR(CLR), .LD(LD), .Count(n1_bit_register_1_c_out), .D(D[1]), .Q(Q[1]), .Clk(Clk),
    .C_OUT(n1_bit_register_5_c_out));
  _1_bit_Register u_1_bit_register_6 (
    .CLR(CLR), .LD(LD), .Count(n1_bit_register_2_c_out), .D(D[5]), .Q(Q[5]), .Clk(Clk),
    .C_OUT(n1_bit_register_6_c_out));
  _1_bit_Register u_1_bit_register_7 (
    .CLR(CLR), .LD(LD), .Count(n1_bit_register_3_c_out), .D(D[9]), .Q(Q[9]), .Clk(Clk),
    .C_OUT(n1_bit_register_7_c_out));
  _1_bit_Register u_1_bit_register_8 (
    .CLR(CLR), .LD(LD), .Count(n1_bit_register_4_c_out), .D(D[13]), .Q(Q[13]), .Clk(Clk),
    .C_OUT(n1_bit_register_8_c_out));
  _1_bit_Register u_1_bit_register_9 (
    .CLR(CLR), .LD(LD), .Count(n1_bit_register_5_c_out), .D(D[2]), .Q(Q[2]), .Clk(Clk),
    .C_OUT(n1_bit_register_9_c_out));
  _1_bit_Register u_1_bit_register_10 (
    .CLR(CLR), .LD(LD), .Count(n1_bit_register_6_c_out), .D(D[6]), .Q(Q[6]), .Clk(Clk),
    .C_OUT(n1_bit_register_10_c_out));
  _1_bit_Register u_1_bit_register_11 (
    .CLR(CLR), .LD(LD), .Count(n1_bit_register_7_c_out), .D(D[10]), .Q(Q[10]), .Clk(Clk),
    .C_OUT(n1_bit_register_11_c_out));
  _1_bit_Register u_1_bit_register_12 (
    .CLR(CLR), .LD(LD), .Count(n1_bit_register_8_c_out), .D(D[14]), .Q(Q[14]), .Clk(Clk),
    .C_OUT(n1_bit_register_12_c_out));
  _1_bit_Register u_1_bit_register_13 (
    .CLR(CLR), .LD(LD), .Count(n1_bit_register_9_c_out), .D(D[3]), .Q(Q[3]), .Clk(Clk),
    .C_OUT(n1_bit_register_13_c_out));
  _1_bit_Register u_1_bit_register_14 (
    .CLR(CLR), .LD(LD), .Count(n1_bit_register_10_c_out), .D(D[7]), .Q(Q[7]), .Clk(Clk),
    .C_OUT(n1_bit_register_14_c_out));
  _1_bit_Register u_1_bit_register_15 (
    .CLR(CLR), .LD(LD), .Count(n1_bit_register_11_c_out), .D(D[11]), .Q(Q[11]), .Clk(Clk),
    .C_OUT(n1_bit_register_15_c_out));
  _1_bit_Register u_1_bit_register_16 (
    .CLR(CLR), .LD(LD), .Count(n1_bit_register_12_c_out), .D(D[15]), .Q(Q[15]), .Clk(Clk));  // open: C_OUT
endmodule

module _12_bit_Register (
  input  CLR,
  input  Count,
  input  LD,
  input  [11:0] D,
  input  Clk,
  output [11:0] Q
);

  wire n1_bit_register_1_c_out, n1_bit_register_2_c_out, n1_bit_register_3_c_out, n1_bit_register_4_c_out,
       n1_bit_register_5_c_out, n1_bit_register_6_c_out, n1_bit_register_7_c_out, n1_bit_register_8_c_out,
       n1_bit_register_9_c_out, n1_bit_register_10_c_out, n1_bit_register_11_c_out;

  _1_bit_Register u_1_bit_register_1 (
    .CLR(CLR), .LD(LD), .Count(Count), .D(D[0]), .Q(Q[0]), .Clk(Clk), .C_OUT(n1_bit_register_1_c_out));
  _1_bit_Register u_1_bit_register_2 (
    .CLR(CLR), .LD(LD), .Count(n1_bit_register_10_c_out), .D(D[4]), .Q(Q[4]), .Clk(Clk),
    .C_OUT(n1_bit_register_2_c_out));
  _1_bit_Register u_1_bit_register_3 (
    .CLR(CLR), .LD(LD), .Count(n1_bit_register_11_c_out), .D(D[8]), .Q(Q[8]), .Clk(Clk),
    .C_OUT(n1_bit_register_3_c_out));
  _1_bit_Register u_1_bit_register_4 (
    .CLR(CLR), .LD(LD), .Count(n1_bit_register_1_c_out), .D(D[1]), .Q(Q[1]), .Clk(Clk),
    .C_OUT(n1_bit_register_4_c_out));
  _1_bit_Register u_1_bit_register_5 (
    .CLR(CLR), .LD(LD), .Count(n1_bit_register_2_c_out), .D(D[5]), .Q(Q[5]), .Clk(Clk),
    .C_OUT(n1_bit_register_5_c_out));
  _1_bit_Register u_1_bit_register_6 (
    .CLR(CLR), .LD(LD), .Count(n1_bit_register_3_c_out), .D(D[9]), .Q(Q[9]), .Clk(Clk),
    .C_OUT(n1_bit_register_6_c_out));
  _1_bit_Register u_1_bit_register_7 (
    .CLR(CLR), .LD(LD), .Count(n1_bit_register_4_c_out), .D(D[2]), .Q(Q[2]), .Clk(Clk),
    .C_OUT(n1_bit_register_7_c_out));
  _1_bit_Register u_1_bit_register_8 (
    .CLR(CLR), .LD(LD), .Count(n1_bit_register_5_c_out), .D(D[6]), .Q(Q[6]), .Clk(Clk),
    .C_OUT(n1_bit_register_8_c_out));
  _1_bit_Register u_1_bit_register_9 (
    .CLR(CLR), .LD(LD), .Count(n1_bit_register_6_c_out), .D(D[10]), .Q(Q[10]), .Clk(Clk),
    .C_OUT(n1_bit_register_9_c_out));
  _1_bit_Register u_1_bit_register_10 (
    .CLR(CLR), .LD(LD), .Count(n1_bit_register_7_c_out), .D(D[3]), .Q(Q[3]), .Clk(Clk),
    .C_OUT(n1_bit_register_10_c_out));
  _1_bit_Register u_1_bit_register_11 (
    .CLR(CLR), .LD(LD), .Count(n1_bit_register_8_c_out), .D(D[7]), .Q(Q[7]), .Clk(Clk),
    .C_OUT(n1_bit_register_11_c_out));
  _1_bit_Register u_1_bit_register_12 (
    .CLR(CLR), .LD(LD), .Count(n1_bit_register_9_c_out), .D(D[11]), .Q(Q[11]), .Clk(Clk));  // open: C_OUT
endmodule

module HA (
  input  A,
  input  B,
  output SUM,
  output CARRY
);

  xor xor_1 (SUM, A, B);
  and and_1 (CARRY, A, B);
endmodule

module FA (
  input  C_IN,
  input  A,
  input  B,
  output SUM,
  output C_OUT
);

  wire ha_1_carry, ha_1_sum, ha_2_carry;

  HA ha_1 (.A(A), .B(B), .SUM(ha_1_sum), .CARRY(ha_1_carry));
  HA ha_2 (.A(C_IN), .B(ha_1_sum), .SUM(SUM), .CARRY(ha_2_carry));
  or or_1 (C_OUT, ha_2_carry, ha_1_carry);
endmodule

module _1_bit_ALU (
  input  AND,
  input  DR_i,
  input  AC_i,
  input  C_i,
  input  ADD,
  input  DR,
  input  INPR,
  input  INPR_i,
  input  CMA,
  input  SHR,
  input  AC_i_1,
  input  SHL,
  input  AC_i_1_2,
  output C_i_1,
  output AC_i_2
);

  wire ADD_out, AND_out, COM_out, DR_out, fa_1_sum, INPR_out, not_1_out, SHL_out, SHR_out;

  FA fa_1 (.A(AC_i), .B(DR_i), .C_IN(C_i), .SUM(fa_1_sum), .C_OUT(C_i_1));
  not not_1 (not_1_out, AC_i);
  and u_AND (AND_out, AND, DR_i, AC_i);
  and u_ADD (ADD_out, fa_1_sum, ADD);
  and u_DR (DR_out, DR_i, DR);
  and u_INPR (INPR_out, INPR, INPR_i);
  and COM (COM_out, not_1_out, CMA);
  and u_SHR (SHR_out, SHR, AC_i_1);
  and u_SHL (SHL_out, SHL, AC_i_1_2);
  or or_1 (AC_i_2, AND_out, ADD_out, DR_out, INPR_out, COM_out, SHR_out, SHL_out);
endmodule

module _16_bit_ALU (
  input  [15:0] AC,
  input  [15:0] DR,
  input  [7:0] INPR,
  input  INPR_IN,
  input  COM,
  input  SHR,
  input  SHL,
  input  E_IN,
  input  AND,
  input  ADD,
  input  DR_IN,
  output [15:0] AC_OUT,
  output E_OUT
);

  wire and_1_out, and_2_out, and_3_out, C_OUT, n1_bit_alu_1_c_i_1, n1_bit_alu_2_c_i_1, n1_bit_alu_3_c_i_1,
       n1_bit_alu_4_c_i_1, n1_bit_alu_5_c_i_1, n1_bit_alu_6_c_i_1, n1_bit_alu_7_c_i_1, n1_bit_alu_8_c_i_1,
       n1_bit_alu_9_c_i_1, n1_bit_alu_10_c_i_1, n1_bit_alu_11_c_i_1, n1_bit_alu_12_c_i_1,
       n1_bit_alu_13_c_i_1, n1_bit_alu_14_c_i_1, n1_bit_alu_15_c_i_1;

  and and_1 (and_1_out, AC[0], SHR);
  and and_2 (and_2_out, AC[15], SHL);
  and and_3 (and_3_out, C_OUT, ADD);
  or or_1 (E_OUT, and_1_out, and_2_out, and_3_out);
  _1_bit_ALU u_1_bit_alu_1 (
    .AND(AND), .DR_i(DR[0]), .AC_i(AC[0]), .C_i(1'b0), .ADD(ADD), .DR(DR_IN), .INPR(INPR_IN),
    .INPR_i(INPR[0]), .CMA(COM), .SHR(SHR), .AC_i_1(AC[1]), .SHL(SHL), .AC_i_1_2(E_IN),
    .C_i_1(n1_bit_alu_1_c_i_1), .AC_i_2(AC_OUT[0]));
  _1_bit_ALU u_1_bit_alu_2 (
    .AND(AND), .DR_i(DR[4]), .AC_i(AC[4]), .C_i(n1_bit_alu_13_c_i_1), .ADD(ADD), .DR(DR_IN), .INPR(INPR_IN),
    .INPR_i(INPR[4]), .CMA(COM), .SHR(SHR), .AC_i_1(AC[5]), .SHL(SHL), .AC_i_1_2(AC[3]),
    .C_i_1(n1_bit_alu_2_c_i_1), .AC_i_2(AC_OUT[4]));
  _1_bit_ALU u_1_bit_alu_3 (
    .AND(AND), .DR_i(DR[8]), .AC_i(AC[8]), .C_i(n1_bit_alu_14_c_i_1), .ADD(ADD), .DR(DR_IN), .INPR(INPR_IN),
    .INPR_i(1'b0), .CMA(COM), .SHR(SHR), .AC_i_1(AC[9]), .SHL(SHL), .AC_i_1_2(AC[7]),
    .C_i_1(n1_bit_alu_3_c_i_1), .AC_i_2(AC_OUT[8]));
  _1_bit_ALU u_1_bit_alu_4 (
    .AND(AND), .DR_i(DR[12]), .AC_i(AC[12]), .C_i(n1_bit_alu_15_c_i_1), .ADD(ADD), .DR(DR_IN),
    .INPR(INPR_IN), .INPR_i(1'b0), .CMA(COM), .SHR(SHR), .AC_i_1(AC[13]), .SHL(SHL), .AC_i_1_2(AC[11]),
    .C_i_1(n1_bit_alu_4_c_i_1), .AC_i_2(AC_OUT[12]));
  _1_bit_ALU u_1_bit_alu_5 (
    .AND(AND), .DR_i(DR[1]), .AC_i(AC[1]), .C_i(n1_bit_alu_1_c_i_1), .ADD(ADD), .DR(DR_IN), .INPR(INPR_IN),
    .INPR_i(INPR[1]), .CMA(COM), .SHR(SHR), .AC_i_1(AC[2]), .SHL(SHL), .AC_i_1_2(AC[0]),
    .C_i_1(n1_bit_alu_5_c_i_1), .AC_i_2(AC_OUT[1]));
  _1_bit_ALU u_1_bit_alu_6 (
    .AND(AND), .DR_i(DR[5]), .AC_i(AC[5]), .C_i(n1_bit_alu_2_c_i_1), .ADD(ADD), .DR(DR_IN), .INPR(INPR_IN),
    .INPR_i(INPR[5]), .CMA(COM), .SHR(SHR), .AC_i_1(AC[6]), .SHL(SHL), .AC_i_1_2(AC[4]),
    .C_i_1(n1_bit_alu_6_c_i_1), .AC_i_2(AC_OUT[5]));
  _1_bit_ALU u_1_bit_alu_7 (
    .AND(AND), .DR_i(DR[9]), .AC_i(AC[9]), .C_i(n1_bit_alu_3_c_i_1), .ADD(ADD), .DR(DR_IN), .INPR(INPR_IN),
    .INPR_i(1'b0), .CMA(COM), .SHR(SHR), .AC_i_1(AC[10]), .SHL(SHL), .AC_i_1_2(AC[8]),
    .C_i_1(n1_bit_alu_7_c_i_1), .AC_i_2(AC_OUT[9]));
  _1_bit_ALU u_1_bit_alu_8 (
    .AND(AND), .DR_i(DR[13]), .AC_i(AC[13]), .C_i(n1_bit_alu_4_c_i_1), .ADD(ADD), .DR(DR_IN), .INPR(INPR_IN),
    .INPR_i(1'b0), .CMA(COM), .SHR(SHR), .AC_i_1(AC[14]), .SHL(SHL), .AC_i_1_2(AC[12]),
    .C_i_1(n1_bit_alu_8_c_i_1), .AC_i_2(AC_OUT[13]));
  _1_bit_ALU u_1_bit_alu_9 (
    .AND(AND), .DR_i(DR[2]), .AC_i(AC[2]), .C_i(n1_bit_alu_5_c_i_1), .ADD(ADD), .DR(DR_IN), .INPR(INPR_IN),
    .INPR_i(INPR[2]), .CMA(COM), .SHR(SHR), .AC_i_1(AC[3]), .SHL(SHL), .AC_i_1_2(AC[1]),
    .C_i_1(n1_bit_alu_9_c_i_1), .AC_i_2(AC_OUT[2]));
  _1_bit_ALU u_1_bit_alu_10 (
    .AND(AND), .DR_i(DR[6]), .AC_i(AC[6]), .C_i(n1_bit_alu_6_c_i_1), .ADD(ADD), .DR(DR_IN), .INPR(INPR_IN),
    .INPR_i(INPR[6]), .CMA(COM), .SHR(SHR), .AC_i_1(AC[7]), .SHL(SHL), .AC_i_1_2(AC[5]),
    .C_i_1(n1_bit_alu_10_c_i_1), .AC_i_2(AC_OUT[6]));
  _1_bit_ALU u_1_bit_alu_11 (
    .AND(AND), .DR_i(DR[10]), .AC_i(AC[10]), .C_i(n1_bit_alu_7_c_i_1), .ADD(ADD), .DR(DR_IN), .INPR(INPR_IN),
    .INPR_i(1'b0), .CMA(COM), .SHR(SHR), .AC_i_1(AC[11]), .SHL(SHL), .AC_i_1_2(AC[9]),
    .C_i_1(n1_bit_alu_11_c_i_1), .AC_i_2(AC_OUT[10]));
  _1_bit_ALU u_1_bit_alu_12 (
    .AND(AND), .DR_i(DR[14]), .AC_i(AC[14]), .C_i(n1_bit_alu_8_c_i_1), .ADD(ADD), .DR(DR_IN), .INPR(INPR_IN),
    .INPR_i(1'b0), .CMA(COM), .SHR(SHR), .AC_i_1(AC[15]), .SHL(SHL), .AC_i_1_2(AC[13]),
    .C_i_1(n1_bit_alu_12_c_i_1), .AC_i_2(AC_OUT[14]));
  _1_bit_ALU u_1_bit_alu_13 (
    .AND(AND), .DR_i(DR[3]), .AC_i(AC[3]), .C_i(n1_bit_alu_9_c_i_1), .ADD(ADD), .DR(DR_IN), .INPR(INPR_IN),
    .INPR_i(INPR[3]), .CMA(COM), .SHR(SHR), .AC_i_1(AC[4]), .SHL(SHL), .AC_i_1_2(AC[2]),
    .C_i_1(n1_bit_alu_13_c_i_1), .AC_i_2(AC_OUT[3]));
  _1_bit_ALU u_1_bit_alu_14 (
    .AND(AND), .DR_i(DR[7]), .AC_i(AC[7]), .C_i(n1_bit_alu_10_c_i_1), .ADD(ADD), .DR(DR_IN), .INPR(INPR_IN),
    .INPR_i(INPR[7]), .CMA(COM), .SHR(SHR), .AC_i_1(AC[8]), .SHL(SHL), .AC_i_1_2(AC[6]),
    .C_i_1(n1_bit_alu_14_c_i_1), .AC_i_2(AC_OUT[7]));
  _1_bit_ALU u_1_bit_alu_15 (
    .AND(AND), .DR_i(DR[11]), .AC_i(AC[11]), .C_i(n1_bit_alu_11_c_i_1), .ADD(ADD), .DR(DR_IN),
    .INPR(INPR_IN), .INPR_i(1'b0), .CMA(COM), .SHR(SHR), .AC_i_1(AC[12]), .SHL(SHL), .AC_i_1_2(AC[10]),
    .C_i_1(n1_bit_alu_15_c_i_1), .AC_i_2(AC_OUT[11]));
  _1_bit_ALU u_1_bit_alu_16 (
    .AND(AND), .DR_i(DR[15]), .AC_i(AC[15]), .C_i(n1_bit_alu_12_c_i_1), .ADD(ADD), .DR(DR_IN),
    .INPR(INPR_IN), .INPR_i(1'b0), .CMA(COM), .SHR(SHR), .AC_i_1(E_IN), .SHL(SHL), .AC_i_1_2(AC[14]),
    .C_i_1(C_OUT), .AC_i_2(AC_OUT[15]));

  // Other names for the same wires on the sheet: DR_t = DR_IN; E = E_IN; INPR_t = INPR_IN
endmodule

module Control_Unit (
  input  [15:0] IR,
  input  Clk,
  input  FGO,
  input  FGI,
  input  IEN,
  input  R,
  input  E,
  input  [15:0] AC,
  input  [15:0] DR,
  output IR_LD,
  output AR_LD,
  output DR_LD,
  output AND,
  output ADD,
  output DR_IN,
  output INPR,
  output COM,
  output SHR,
  output SHL,
  output MEM_WRITE,
  output DR_INR,
  output AR_CLR,
  output TR_LD,
  output AR_INR,
  output FGI_CLR,
  output S0,
  output OUTR_LD,
  output S1,
  output FGO_CLR,
  output S2,
  output PC_LD,
  output R_SET,
  output AC_LD,
  output E_CLR,
  output MEM_READ,
  output PC_INR,
  output E_COM,
  output R_CLR,
  output S_CLR,
  output AC_INR,
  output IEN_CLR,
  output AC_CLR,
  output IEN_SET,
  output PC_CLR,
  output E_LD
);

  wire I, SC_CLR;
  wire [3:0] SC_q;
  wire [7:0] D0_D7, T0_T7;

  Counter #(.width(4), .max('hf)) SC (.count(1'b1), .Q(SC_q), .clk(Clk), .clr(SC_CLR));  // open: load, D, carry
  Decoder #(.select(3)) decoder_1 (
    .out0(D0_D7[0]), .out1(D0_D7[1]), .out2(D0_D7[2]), .out3(D0_D7[3]), .out4(D0_D7[4]), .out5(D0_D7[5]),
    .out6(D0_D7[6]), .out7(D0_D7[7]), .sel(IR[14:12]), .en(1'b1));
  D_Flip_Flop u_I (.clk(Clk), .D(IR[15]), .Q(I), .en(1'b1));  // open: Qn, preset, reset
  Decoder #(.select(4)) decoder_2 (
    .out0(T0_T7[0]), .out1(T0_T7[1]), .out2(T0_T7[2]), .out3(T0_T7[3]), .out4(T0_T7[4]), .out5(T0_T7[5]),
    .out6(T0_T7[6]), .out7(T0_T7[7]), .sel(SC_q), .en(1'b1));  // open: out8, out9, out10, out11, out12, out13, out14, out15
  CONTROL_GATES control_gates_1 (
    .T0(T0_T7[0]), .T1(T0_T7[1]), .T2(T0_T7[2]), .T3(T0_T7[3]), .T4(T0_T7[4]), .T5(T0_T7[5]), .T6(T0_T7[6]),
    .T7(T0_T7[7]), .I(I), .D0(D0_D7[0]), .D1(D0_D7[1]), .D2(D0_D7[2]), .D3(D0_D7[3]), .D4(D0_D7[4]),
    .D5(D0_D7[5]), .D6(D0_D7[6]), .D7(D0_D7[7]), .B0(IR[0]), .B1(IR[1]), .B2(IR[2]), .B3(IR[3]), .B4(IR[4]),
    .B5(IR[5]), .B6(IR[6]), .B7(IR[7]), .B8(IR[8]), .B9(IR[9]), .B10(IR[10]), .B11(IR[11]), .R(R), .E(E),
    .AC(AC), .IEN(IEN), .FGI(FGI), .FGO(FGO), .DR(DR), .IR_LD(IR_LD), .AR_LD(AR_LD), .DR_LD(DR_LD),
    .SC_CLR(SC_CLR), .MEM_WRITE(MEM_WRITE), .DR_INR(DR_INR), .AR_CLR(AR_CLR), .TR_LD(TR_LD), .AR_INR(AR_INR),
    .FGI_CLR(FGI_CLR), .OUTR_LD(OUTR_LD), .FGO_CLR(FGO_CLR), .PC_LD(PC_LD), .R_SET(R_SET), .AC_LD(AC_LD),
    .E_CLR(E_CLR), .MEM_READ(MEM_READ), .PC_INR(PC_INR), .E_COM(E_COM), .R_CLR(R_CLR), .S_CLR(S_CLR),
    .AC_INR(AC_INR), .IEN_CLR(IEN_CLR), .AC_CLR(AC_CLR), .IEN_SET(IEN_SET), .PC_CLR(PC_CLR), .AND(AND),
    .ADD(ADD), .DR_2(DR_IN), .INPR(INPR), .SHR(SHR), .SHL(SHL), .E_LD(E_LD), .COM(COM), .S0(S0), .S1(S1),
    .S2(S2));

  // Other names for the same wires on the sheet: B0_B11[11:0] = IR[11:0]
endmodule

module CONTROL_GATES (
  input  T0,
  input  T1,
  input  T2,
  input  T3,
  input  T4,
  input  T5,
  input  T6,
  input  T7,
  input  I,
  input  D0,
  input  D1,
  input  D2,
  input  D3,
  input  D4,
  input  D5,
  input  D6,
  input  D7,
  input  B0,
  input  B1,
  input  B2,
  input  B3,
  input  B4,
  input  B5,
  input  B6,
  input  B7,
  input  B8,
  input  B9,
  input  B10,
  input  B11,
  input  R,
  input  E,
  input  [15:0] AC,
  input  IEN,
  input  FGI,
  input  FGO,
  input  [15:0] DR,
  output AR_LD,
  output AR_INR,
  output AR_CLR,
  output PC_LD,
  output PC_INR,
  output PC_CLR,
  output DR_LD,
  output DR_INR,
  output AND,
  output ADD,
  output DR_2,
  output AC_LD,
  output INPR,
  output COM,
  output SHR,
  output SHL,
  output AC_INR,
  output AC_CLR,
  output IR_LD,
  output TR_LD,
  output OUTR_LD,
  output MEM_READ,
  output MEM_WRITE,
  output R_SET,
  output R_CLR,
  output IEN_CLR,
  output IEN_SET,
  output SC_CLR,
  output FGI_CLR,
  output FGO_CLR,
  output E_CLR,
  output E_COM,
  output S_CLR,
  output E_LD,
  output S0,
  output S1,
  output S2
);

  wire AC_0, and_12_out, and_13_out, and_14_out, and_15_out, and_17_out, and_18_out, and_19_out, and_24_out,
       and_25_out, and_26_out, and_28_out, and_29_out, and_30_out, and_31_out, and_32_out, and_33_out,
       and_39_out, and_40_out, and_41_out, and_42_out, and_43_out, and_44_out, and_46_out, and_47_out,
       and_49_out, and_50_out, and_51_out, and_52_out, and_53_out, and_54_out, and_55_out, and_56_out,
       and_57_out, and_58_out, and_59_out, and_60_out, and_62_out, and_63_out, and_64_out, and_67_out, DR_0,
       not_1_out, not_2_out, not_3_out, not_4_out, not_5_out, not_6_out, not_7_out, not_8_out, not_9_out,
       not_10_out, not_11_out, not_12_out, not_13_out, not_14_out, or_1_out, or_2_out, or_3_out, or_4_out,
       or_5_out, p, r_t, x1, x2, x3, x4, x5, x6;

  not not_1 (not_1_out, I);
  nor nor_1 (AC_0, AC[7], AC[0], AC[1], AC[2], AC[3], AC[4], AC[5], AC[6], AC[8], AC[9], AC[10], AC[11], AC[12], AC[13], AC[14], AC[15]);
  nor nor_2 (DR_0, DR[7], DR[0], DR[1], DR[2], DR[3], DR[4], DR[5], DR[6], DR[8], DR[9], DR[10], DR[11], DR[12], DR[13], DR[14], DR[15]);
  and and_1 (r_t, D7, not_1_out, T3);
  and and_2 (p, D7, I, T3);
  not not_2 (not_2_out, R);
  not not_3 (not_3_out, R);
  not not_4 (not_4_out, D7);
  not not_5 (not_5_out, R);
  not not_6 (not_6_out, D7);
  not not_7 (not_7_out, R);
  not not_8 (not_8_out, AC[15]);
  not not_9 (not_9_out, E);
  and and_3 (AND, D0, T5);
  and and_4 (ADD, T5, D1);
  and and_5 (DR_2, D2, T5);
  and and_6 (INPR, p, B11);
  and and_7 (COM, r_t, B9);
  and and_8 (SHR, r_t, B7);
  and and_9 (SHL, r_t, B6);
  and and_10 (AC_INR, r_t, B5);
  and and_11 (AC_CLR, r_t, B11);
  and and_12 (and_12_out, D3, T4);
  and and_13 (and_13_out, p, B10);
  not not_10 (not_10_out, R);
  not not_11 (not_11_out, R);
  and and_14 (and_14_out, not_2_out, T1);
  and and_15 (and_15_out, not_6_out, I, T3);
  and and_16 (R_CLR, R, T2);
  and and_17 (and_17_out, R, T3);
  or or_1 (or_1_out, D0, D1, D2, D5);
  or or_2 (or_2_out, D3, D4);
  and and_18 (and_18_out, D6, T7);
  and and_19 (and_19_out, D7, T4);
  and and_20 (FGI_CLR, p, B11);
  and and_21 (FGO_CLR, p, B10);
  and and_22 (E_CLR, r_t, B10);
  and and_23 (E_COM, r_t, B8);
  and and_24 (and_24_out, r_t, B7);
  and and_25 (and_25_out, B6, r_t);
  and and_26 (and_26_out, D1, T5);
  and and_27 (AR_CLR, R, T0);
  and and_28 (and_28_out, T4, D4);
  and and_29 (and_29_out, D5, T5);
  and and_30 (and_30_out, D4, T4);
  and and_31 (and_31_out, D5, T5);
  or or_3 (or_3_out, D0, D1, D2, D6);
  and and_32 (and_32_out, D2, T5);
  and and_33 (and_33_out, D6, T6);
  and and_34 (IR_LD, not_10_out, T1);
  and and_35 (x5, not_11_out, T2);
  and and_36 (TR_LD, R, T0);
  and and_37 (x6, R, T1);
  and and_38 (OUTR_LD, p, B10);
  or or_4 (or_4_out, D0, D1, D2, D6);
  and and_39 (and_39_out, R, T1);
  and and_40 (and_40_out, D3, T4);
  and and_41 (and_41_out, D5, T4);
  and and_42 (and_42_out, D6, T6);
  not not_12 (not_12_out, T0);
  not not_13 (not_13_out, T1);
  not not_14 (not_14_out, T2);
  or or_5 (or_5_out, FGI, FGO);
  and and_43 (and_43_out, R, T2);
  and and_44 (and_44_out, p, B6);
  and and_45 (IEN_SET, p, B7);
  and and_46 (and_46_out, or_1_out, T6);
  and and_47 (and_47_out, or_2_out, T5);
  and and_48 (S_CLR, r_t, B0);
  or or_6 (S0, x1, x3, x5, MEM_READ);
  or or_7 (S1, x2, x3, x6, MEM_READ);
  or or_8 (S2, x4, x5, x6, MEM_READ);
  and and_49 (and_49_out, not_3_out, T0);
  and and_50 (and_50_out, not_3_out, T2);
  and and_51 (and_51_out, T3, I, not_4_out);
  and and_52 (and_52_out, not_7_out, T1);
  and and_53 (and_53_out, R, T2);
  and and_54 (and_54_out, DR_0, D6, T6);
  and and_55 (and_55_out, r_t, B4, not_8_out);
  and and_56 (and_56_out, AC[15], r_t, B3);
  and and_57 (and_57_out, r_t, B2, AC_0);
  and and_58 (and_58_out, r_t, B1, not_9_out);
  and and_59 (and_59_out, p, B9, FGI);
  and and_60 (and_60_out, FGO, B8, p);
  and and_61 (PC_CLR, R, T1);
  and and_62 (and_62_out, T0, not_5_out);
  and and_63 (and_63_out, T0, R);
  and and_64 (and_64_out, D5, T4);
  and and_65 (DR_LD, T4, or_3_out);
  and and_66 (DR_INR, D6, T5);
  or or_9 (x3, and_32_out, and_33_out);
  or or_10 (x4, and_12_out, and_13_out);
  and and_67 (and_67_out, or_4_out, T4);
  and and_68 (R_SET, not_12_out, not_13_out, not_14_out, IEN, or_5_out);
  or or_11 (IEN_CLR, and_43_out, and_44_out);
  or or_12 (E_LD, and_24_out, and_25_out, and_26_out);
  or or_13 (AR_LD, and_49_out, and_50_out, and_51_out);
  and and_69 (AR_INR, D5, T4);
  or or_14 (x1, and_28_out, and_29_out);
  or or_15 (AC_LD, AND, ADD, DR_2, INPR, COM, SHR, SHL);
  or or_16 (MEM_READ, and_14_out, and_15_out, and_67_out);
  or or_17 (MEM_WRITE, and_39_out, and_40_out, and_41_out, and_42_out);
  or or_18 (PC_LD, and_30_out, and_31_out);
  or or_19 (PC_INR, and_52_out, and_53_out, and_54_out, and_55_out, and_56_out, and_57_out, and_58_out, and_59_out, and_60_out);
  or or_20 (x2, and_62_out, and_63_out, and_64_out);
  or or_21 (SC_CLR, and_17_out, and_46_out, and_47_out, and_18_out, and_19_out);

  // Other names for the same wires on the sheet: x7 = MEM_READ

  // Notes on the sheet:
  //   SC
  //   E
  //   S-BUS
  //   AR
  //   PC
  //   DR
  //   AC
  //   IR
  //   TR
  //   OUTR
  //   READ
  //   WRITE
  //   R
  //   IEN
  //   FGI
  //   FGO
  //   E
  //   S
endmodule
